# Fritzing sketch DivisorResistivoPotenciometro (saved by Fritzing 0.9.3b)
breadboards: 1

parts:
  R2 = Resistor [tolerance=±5% resistance=1k package=THT]
  ArduinoUno = Arduino Uno (Rev3)
  R3 = Trimmer Potentiometer [maximum_resistance=10kΩ package=THT]

nets:
  N1: R2.Pin_0, ArduinoUno.A0, R3.leg2
  N2: R2.Pin_1, ArduinoUno.GND
  N3: ArduinoUno.5V, R3.leg1, R3.wiper

// code stored in the sketch: DivisorResistivoPotenciometro.ino
#define analogInPin A0

int sensorValue = 0;

void setup() {
  Serial.begin(9600); 
}

void loop() {
  sensorValue = analogRead(analogInPin);
  Serial.print("Potenc = " );            
  Serial.println(sensorValue);      
  delay(500);                     
}
