# Fritzing sketch MedidorDeTensao (saved by Fritzing 0.9.3b)
breadboards: 1

parts:
  ArduinoUno = Arduino Uno (Rev3)
  R2 = Resistor [tolerance=±5% resistance=10k package=THT]
  R1_??? = Resistor [tolerance=±5% resistance=220 package=THT]

nets:
  N1: ArduinoUno.A0, R2.Pin_1, R1_???.Pin_0
  N2: ArduinoUno.GND, R2.Pin_0
  N3: ArduinoUno.5V, R1_???.Pin_1

// code stored in the sketch: exemplo_11.ino
#define RESIST_PIN   A0
float Vin;
float R1;
float Vref = 5;
float Steps=1023;
float StepSize = (float)Vref/(float)Steps;
float R2 = 10000;

void setup() {
  Serial.begin(9600);
  Serial.println("Ready");
}

void loop() {
  ADC=analogRead(RESIST_PIN);
  Vin = StepSize*(float)ADC;
  /*
  Vout = (Vin*R2)/(R1+R2)
  R1 = ((Vin-Vout)*R2)/(Vout)
  */
  R1 = (float)((5-Vin)*10000)/(float)Vin;
  Serial.println(R1);
  delay(300);
}
