# Fritzing sketch Botao (saved by Fritzing 0.9.3b)
breadboards: 1

parts:
  ArduinoUno = Arduino Uno (Rev3)
  S1 = Pushbutton [package="[THT]"]

nets:
  N1: ArduinoUno.GND, S1.Pin_3, S1.Pin_4
  N2: ArduinoUno.D2, S1.Pin_1, S1.Pin_2

// code stored in the sketch: exemplo_4.ino
int ledPin = 13;
int buttonPin = 2;
int flag = LOW;
void setup(){
  pinMode(ledPin, OUTPUT);
  pinMode(buttonPin, INPUT);
	digitalWrite(buttonPin, HIGH);//Ativa o resitor de pull up
}
void loop(){
  int button = digitalRead(buttonPin);
  if (button==HIGH){
    delay(300);
    button = digitalRead(buttonPin);
    if (button==HIGH)
      flag = HIGH;
  }
  else{
    delay(300);
    button = digitalRead(buttonPin);
    if (button==LOW)
      flag = LOW;
  }
  if(flag)
    digitalWrite(ledPin,HIGH);
  else
    digitalWrite(ledPin, LOW);
}

// code stored in the sketch: exemplo_4_bounce.ino
#include <Bounce2.h>//https://github.com/thomasfredericks/Bounce2

int ledPin = 13;
int buttonPin = 2;
Bounce  bouncer  = Bounce();

void setup()
{
  pinMode(ledPin, OUTPUT);
  pinMode(buttonPin, INPUT);
	digitalWrite(buttonPin, HIGH);//Ativa o resitor de pull up
	bouncer.attach( inputPin );
	bouncer.interval(5);
}
int flag = 0;
void loop()
{ 
  debouncer.update();
  flag = debouncer.read();
  
  if(flag)
    digitalWrite(ledPin,HIGH);
  else
    digitalWrite(ledPin, LOW);
}
