# Fritzing sketch PWM_ReleEstadoSolido (saved by Fritzing 0.9.3b)
breadboards: 1

parts:
  ArduinoUno = Arduino Uno (Rev3)
  LED1 = LED - 5mm [color="Red (633nm)" package="5 mm [THT]"]
  R1 = Resistor [tolerance=±5% resistance=470 package=THT]

nets:
  N1: ArduinoUno.GND, LED1.cathode
  N2: ArduinoUno.D5_PWM, R1.Pin_1
  N3: LED1.anode, R1.Pin_0
