# Fritzing sketch Ponte H-H (saved by Fritzing 0.9.3b)
breadboards: 1

parts:
  ArduinoUno = Arduino Uno (Rev3)
  S1 = H-Bridge with L298N
  VCC1 = 4 x AAA Battery Mount
  M1 = DC Motor
  M2 = DC Motor

nets:
  N1: ArduinoUno.D10_PWM/SS, S1.IN3
  N2: ArduinoUno.D11_PWM/MOSI, S1.IN4
  GND: ArduinoUno.GND, S1.GND, VCC1.-
  N3: ArduinoUno.D5_PWM, S1.IN1
  N4: ArduinoUno.D6_PWM, S1.IN2
  N5: S1.5V, VCC1.+
  N6: S1.OUT3-Motor2, M1.pin_2
  N7: S1.OUT4-Motor2, M1.pin_1
  N8: S1.OUT1-Motor1, M2.pin_2
  N9: S1.OUT2-Motor1, M2.pin_1

custom parts:
  H-Bridge with L298N: h-bridge

// code stored in the sketch: exemplo_16.ino
int IN1 = 5 ; int IN2 = 6;//motor A
int IN3 = 10; int IN4 = 7;//motor B
int velocidade = 0;
void setup(){
  pinMode(IN1,OUTPUT);
  pinMode(IN2,OUTPUT);
  pinMode(IN3,OUTPUT);
  pinMode(IN4,OUTPUT);
}
void loop(){
  digitalWrite(IN2,LOW);//Sentido Horario 
  digitalWrite(IN1,230);//Alta
  digitalWrite(IN1,150);//Intermediaria
  digitalWrite(IN1,80);//Baixa
  digitalWrite(IN4,LOW);//Sentido Horario Motor B
  while (velocidade < 255){//velocidade de 0 a 255
    digitalWrite(IN3,velocidade);
    velocidade = velocidade + 10;
    delay(50);
  }
  while (velocidade > 0){//velocidade de 255 a 0
    digitalWrite(IN3,velocidade);
    velocidade = velocidade - 10;
    delay(50);
  }
}
